# Fritzing sketch Fritzing scheme (saved by Fritzing 0.9.3b)

parts:
  BMP280_Breakout1 = BMP280 Breakout Board [part_number=BMP280]
  U2 = NodeMCU V1.0
  MH-Z19 = MH-Z19 CO2 Sensor [chip_label=? package=THT]

nets:
  VCC: BMP280_Breakout1.VCC, U2.3V3
  GND: BMP280_Breakout1.GND, U2.GND, MH-Z19.GND
  N1: BMP280_Breakout1.SCL, U2.D2
  N2: BMP280_Breakout1.SDA, U2.D1
  N3: BMP280_Breakout1.CSB, U2.D4
  N4: BMP280_Breakout1.SDO, U2.D3
  N5: U2.D5, MH-Z19.Tx
  N6: U2.D6, MH-Z19.Rx
  VIN: U2.Vin, MH-Z19.Vin

custom parts:
  BMP280 Breakout Board: This is a breakout board for the Bosch Sensortec BMP280, "an absolute barometric pressure sensor especially designed for mobile applications." The operation range is 300 to 1100 hPa. Supply voltage is 1.2 to 3.6V. Operating temperature range is -40 to +85 °C.
  NodeMCU V1.0: ESP8266 based NodeMCU
